# Fritzing sketch MASTER (saved by Fritzing 0.9.2b)

parts:
  Componente1 = Arduino Mega 2560 (Rev3)
  MIRF2 = 2.4GHz Low Power Transceiver [package=qfn20]
  U1 = ESP8266 WiFi Module [part_number=ESP8266]
  R1 = Resistor [tolerance=±5% resistance=10k package=THT]
  R2 = Resistor [tolerance=±5% resistance=20k package=THT]  # not connected
  Componente2 = Barometric Pressure Sensor - BMP085 Breakout
  DHT1 = DHT11 Humitidy and Temperature Sensor
  part = Resistor [tolerance=±5% resistance=10k package=THT]
  10k = Photocell (LDR) [package=THT]

nets:
  N1: Componente1.A0, part.Pin_0, 10k.pin_0
  N2: Componente1.D21/SCL, Componente1.SCL, Componente2.SCL
  N3: Componente1.D20/SDA, Componente1.SDA, Componente2.SDA
  N4: Componente1.D19/RX1, U1.RXD
  N5: Componente1.D18/TX1, R1.Pin_0
  GND: Componente1.GND, Componente2.GND, DHT1.GND, 10k.pin_1
  N6: Componente1.IOREF, part.Pin_1
  5V: Componente1.VIN, MIRF2.VDD, Componente2.VCC, DHT1.VDD
  N7: Componente1.D4_PWM, DHT1.DATA
  N8: Componente1.D48, MIRF2.CE
  N9: Componente1.D49, MIRF2.CSN
  N10: Componente1.D50, MIRF2.MISO
  N11: Componente1.D51, MIRF2.MOSI
  N12: Componente1.D52, MIRF2.SCK
  N13: U1.TXD, R1.Pin_1
  N14: U1.VCC, U1.CH_PD

custom parts:
  ESP8266 WiFi Module: Generic WiFi Module based on the ESP8266 with onboard PCB antenna and UART communications
  DHT11 Humitidy and Temperature Sensor: DHT11 Humidity and Temperature Sensor
