# Fritzing sketch PLANT (saved by Fritzing 0.9.2b)
breadboards: 1

parts:
  X1 = Crystal [frequency="16 Mhz" package=THT]
  C1 = Ceramic Capacitor [capacitance=22pF package="100 mil [THT, multilayer]"]
  C2 = Ceramic Capacitor [capacitance=22pF package="100 mil [THT, multilayer]"]
  U1 = atmega328 [package=dip]
  HIGROMETER = HIH-4030 [package=hih-4030]
  RELE' = RELAY [package=relay-g5q]
  part = Resistor [tolerance=±5% resistance=1k package=THT]
  part_2 = Resistor [tolerance=±5% resistance=10k package=THT]
  Q1 = NPN-Transistor [package="TO92 [THT]"]
  part_3 = Rectifier Diode [part_number=1N4001 package="300 mil [THT]"]
  MIRF1 = 2.4GHz Low Power Transceiver [package=qfn20]
  WATER_PUMP = HIH-4030 [package=hih-4030]

nets:
  N1: X1.pin_1, C1.1, U1.XLAT1
  GND: C1.0, C2.0, U1.GND, HIGROMETER.GND, RELE'.NO, part_2.Pin_0, Q1.E, part_3.anode, WATER_PUMP.GND
  N2: C2.1, U1.XLAT2
  5V: U1.VCC, HIGROMETER.VCC, RELE'.NC, RELE'.COIL1
  N3: U1.D8, part.Pin_1
  N4: U1.D9_(PWM), MIRF1.CE
  N5: U1.D10_(PWM), MIRF1.CSN
  N6: U1.D11_(PWM), MIRF1.MOSI
  N7: U1.D12, MIRF1.MISO
  N8: U1.D13, MIRF1.SCK
  N9: U1.A0, HIGROMETER.OUT
  N10: RELE'.COIL2, Q1.C, part_3.cathode
  N11: RELE'.MAIN, WATER_PUMP.VCC
  N12: part_2.Pin_1, Q1.B
